# Fritzing sketch Greenhouse (saved by Fritzing 1.0.0)

parts:
  Arduino_Uno = Arduino Uno (Rev3)
  Zone_1_soil_/_A0 = Soil Moisture Sensor
  Zone_2_soil_/_A1 = Soil Moisture Sensor
  Outside_light_/_A2 = Photocell (LDR) [package=THT]
  LDR_divider_10k = Resistor [resistance=10k package=THT]
  Inside_light_/_A3 = Photocell (LDR) [package=THT]
  LDR_divider_10k_2 = Resistor [resistance=10k package=THT]
  DS3231_/_0x68 = ZS-042 RTC Module
  20x4_LCD_I2C_0x27 = 20x4 I2C LCD - illustrative 4-pin module
  Auto_mode_/_D3 = SPST Switch [package=switch-spdt]
  Manual_zone_1_/_D4 = Round Pushbutton
  Manual_zone_2_/_D5 = Round Pushbutton
  Tank_empty_/_D6 = SPST Switch [package=switch-spdt]
  Pump_resistor330 = Resistor [resistance=330 package=THT]
  Pump_/_D2_-_330_ohm = Red LED - 5mm [package="5 mm [THT]"]
  Valve1_resistor330 = Resistor [resistance=330 package=THT]
  Valve_1_/_D8_-_330_ohm = Red LED - 5mm [package="5 mm [THT]"]
  Valve2_resistor330 = Resistor [resistance=330 package=THT]
  Valve_2_/_D9_-_330_ohm = Red LED - 5mm [package="5 mm [THT]"]
  Fan_resistor330 = Resistor [resistance=330 package=THT]
  Fan_/_D10_-_330_ohm = Red LED - 5mm [package="5 mm [THT]"]
  Heater_resistor330 = Resistor [resistance=330 package=THT]
  Heater_/_D11_-_330_ohm = Red LED - 5mm [package="5 mm [THT]"]
  GrowLight_resistor330 = Resistor [resistance=330 package=THT]
  Grow_light_/_D12_-_330_ohm = Red LED - 5mm [package="5 mm [THT]"]
  Alarm_resistor330 = Resistor [resistance=330 package=THT]
  Alarm_/_D13_-_330_ohm = Red LED - 5mm [package="5 mm [THT]"]
  DHT22_/_D7 = DHT22 - illustrative external interface
  DHT_DATA_pull-up10k = Resistor [resistance=10k package=THT]

nets:
  N1: Arduino_Uno.A0, Zone_1_soil_/_A0.SIG
  N2: Arduino_Uno.A1, Zone_2_soil_/_A1.SIG
  N3: Arduino_Uno.A2, Outside_light_/_A2.pin_1, LDR_divider_10k.Pin_0
  N4: Arduino_Uno.A3, Inside_light_/_A3.pin_1, LDR_divider_10k_2.Pin_0
  N5: Arduino_Uno.A4/SDA, DS3231_/_0x68.SDA, 20x4_LCD_I2C_0x27.SDA
  N6: Arduino_Uno.A5/SCL, DS3231_/_0x68.SCL, 20x4_LCD_I2C_0x27.SCL
  N7: Arduino_Uno.D8, Valve1_resistor330.Pin_0
  N8: Arduino_Uno.D9_PWM, Valve2_resistor330.Pin_0
  N9: Arduino_Uno.D10_PWM/SS, Fan_resistor330.Pin_0
  N10: Arduino_Uno.D11_PWM/MOSI, Heater_resistor330.Pin_0
  N11: Arduino_Uno.D12/MISO, GrowLight_resistor330.Pin_0
  N12: Arduino_Uno.D13/SCK, Alarm_resistor330.Pin_0
  GND: Arduino_Uno.GND, Zone_1_soil_/_A0.GND, Zone_2_soil_/_A1.GND, LDR_divider_10k.Pin_1, LDR_divider_10k_2.Pin_1, DS3231_/_0x68.GND, 20x4_LCD_I2C_0x27.GND, Auto_mode_/_D3.O, Manual_zone_1_/_D4.leg1, Manual_zone_2_/_D5.leg1, Tank_empty_/_D6.O, Pump_/_D2_-_330_ohm.cathode, Valve_1_/_D8_-_330_ohm.cathode, Valve_2_/_D9_-_330_ohm.cathode, Fan_/_D10_-_330_ohm.cathode, Heater_/_D11_-_330_ohm.cathode, Grow_light_/_D12_-_330_ohm.cathode, Alarm_/_D13_-_330_ohm.cathode, DHT22_/_D7.GND
  N13: Arduino_Uno.D2, Pump_resistor330.Pin_0
  N14: Arduino_Uno.D3_PWM, Auto_mode_/_D3.P
  N15: Arduino_Uno.D4, Manual_zone_1_/_D4.leg0
  N16: Arduino_Uno.D5_PWM, Manual_zone_2_/_D5.leg0
  N17: Arduino_Uno.D6_PWM, Tank_empty_/_D6.P
  N18: Arduino_Uno.D7, DHT22_/_D7.DATA, DHT_DATA_pull-up10k.Pin_1
  VCC: Arduino_Uno.5V, Zone_1_soil_/_A0.VCC, Zone_2_soil_/_A1.VCC, Outside_light_/_A2.pin_0, Inside_light_/_A3.pin_0, DS3231_/_0x68.VCC, 20x4_LCD_I2C_0x27.VCC, DHT22_/_D7.VCC, DHT_DATA_pull-up10k.Pin_0
  N19: Pump_resistor330.Pin_1, Pump_/_D2_-_330_ohm.anode
  N20: Valve1_resistor330.Pin_1, Valve_1_/_D8_-_330_ohm.anode
  N21: Valve2_resistor330.Pin_1, Valve_2_/_D9_-_330_ohm.anode
  N22: Fan_resistor330.Pin_1, Fan_/_D10_-_330_ohm.anode
  N23: Heater_resistor330.Pin_1, Heater_/_D11_-_330_ohm.anode
  N24: GrowLight_resistor330.Pin_1, Grow_light_/_D12_-_330_ohm.anode
  N25: Alarm_resistor330.Pin_1, Alarm_/_D13_-_330_ohm.anode

custom parts:
  20x4 I2C LCD - illustrative 4-pin module: Original teaching representation of an external 20x4 HD44780 LCD with PCF8574 I2C backpack. Verify the labels/order on the actual module. Not a PCB footprint or simulator model.
  DHT22 - illustrative external interface: External four-pin interface only. Not a manufacturer footprint or simulated device.
